# Fritzing sketch MM (saved by Fritzing 0.9.2b)
breadboards: 1

parts:
  J1 = Basic Servo
  Part3 = Arduino Uno (Rev3)
  LCD1 = LCD screen  # not connected
  R1 = Rotary Potentiometer (Small) [maximum_resistance=100kΩ package=THT]  # not connected

nets:
  GND: J1.gnd, Part3.GND
  VCC: J1.vcc, Part3.5V
  N1: J1.pulse, Part3.D9_PWM

// code stored in the sketch: SweepTest.ino
// Sweep
// by BARRAGAN <http://barraganstudio.com> 
// This example code is in the public domain.


#include <Servo.h> 
 
Servo myservo;  // create servo object to control a servo 
                // a maximum of eight servo objects can be created 
 
int pos = 0;    // variable to store the servo position 
 
void setup() 
{ 
  myservo.attach(8);  // attaches the servo on pin 2 to the servo object 
} 
 
 
void loop() 
{ 

    myservo.write(180);              // tell servo to go to position in variable 'pos' 
    delay(2000);                       // waits 15ms for the servo to reach the position 
		myservo.write(0);
    delay(2000);
}
